# Fritzing sketch BH1750 (saved by Fritzing 0.9.3b)

parts:
  ANT1 = Antenna
  Part1 = Adafruit Feather M0 RFM9x LoRa [part_number="Adafruit #3178 or #3179"]
  Part4 = BH1750

nets:
  N1: ANT1.antenna_lead, Part1.ANT
  N2: Part1.DIO1, Part1.D5
  GND: Part1.GND, Part4.GND
  +3V3: Part1.+3V3, Part4.VCC
  N3: Part1.D6, Part1.DIO2
  N4: Part1.SCL, Part4.SCL
  N5: Part1.SDA, Part4.SDA

custom parts:
  Adafruit Feather M0 RFM9x LoRa: This is the Adafruit Feather M0 RFM95 LoRa Radio - our take on an microcontroller with a "Long Range (LoRa)" packet radio transceiver with built in USB and battery charging. Its an Adafruit Feather M0 with a 433Mhz or 900MHz radio module cooked in! Great for making wireless networks that are more flexible than Bluetooth LE and without the high power requirements of WiFi. We have other boards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
  BH1750: Light Sensor
