# Fritzing sketch BMP085-BMP180 (saved by Fritzing 0.9.3b)

parts:
  ANT1 = Antenna
  Part1 = Adafruit Feather M0 RFM9x LoRa [part_number="Adafruit #3178 or #3179"]
  Part2 = Adafruit BMP085 [part_number="Adafruit #391"]

nets:
  N1: ANT1.antenna_lead, Part1.ANT
  N2: Part1.DIO1, Part1.D5
  GND: Part1.GND, Part2.GND
  +3V3: Part1.+3V3, Part2.VIN
  N3: Part1.D6, Part1.DIO2
  N4: Part1.SCL, Part2.SCL
  N5: Part1.SDA, Part2.SDA

custom parts:
  Adafruit Feather M0 RFM9x LoRa: This is the Adafruit Feather M0 RFM95 LoRa Radio - our take on an microcontroller with a "Long Range (LoRa)" packet radio transceiver with built in USB and battery charging. Its an Adafruit Feather M0 with a 433Mhz or 900MHz radio module cooked in! Great for making wireless networks that are more flexible than Bluetooth LE and without the high power requirements of WiFi. We have other boards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
  Adafruit BMP085: This precision sensor from Bosch is the best low-cost sensing solution for measuring barometric pressure and temperature. Because pressure changes with altitude you can also use it as an altimeter! The sensor is soldered onto a PCB with a 3.3V regulator, I2C level shifter and pull-up resistors on the I2C pins. NEW! We now have a fully 5V compliant version of this board - a 3.3V regulator and a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
