# Fritzing sketch TLS2561 (saved by Fritzing 0.9.3b)

parts:
  ANT1 = Antenna
  Part1 = Adafruit Feather M0 RFM9x LoRa [part_number="Adafruit #3178 or #3179"]
  Part3 = Adafruit TSL2561 [part_number="Adafruit #439"]

nets:
  N1: ANT1.antenna_lead, Part1.ANT
  N2: Part1.DIO1, Part1.D5
  GND: Part1.GND, Part3.GND
  +3V3: Part1.+3V3, Part3.VIN
  N3: Part1.D6, Part1.DIO2
  N4: Part1.SCL, Part3.SCL
  N5: Part1.SDA, Part3.SDA

custom parts:
  Adafruit Feather M0 RFM9x LoRa: This is the Adafruit Feather M0 RFM95 LoRa Radio - our take on an microcontroller with a "Long Range (LoRa)" packet radio transceiver with built in USB and battery charging. Its an Adafruit Feather M0 with a 433Mhz or 900MHz radio module cooked in! Great for making wireless networks that are more flexible than Bluetooth LE and without the high power requirements of WiFi. We have other boards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
  Adafruit TSL2561: The TSL2561 luminosity sensor is an advanced digital light sensor, ideal for use in a wide range of light situations. Compared to low cost CdS cells, this sensor is more precise, allowing for exact lux calculations and can be configured for different gain/timing ranges to detect light ranges from up to 0.1 - 40,000+ Lux on the fly. The best part of this sensor is that it contains both infrared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
